// Logisim project alu.circ as structural Verilog: 1 circuit, main circuit alu
module alu (
  input  [31:0] A,
  input  [31:0] B,
  input  [3:0] ALUSel,
  output [31:0] Result
);

  wire [0:0] slt0;
  wire [1:0] multiplexer_2_out, multiplexer_7_out_2, multiplexer_9_out_2;
  wire [3:0] multiplexer_3_out, multiplexer_8_out_2, multiplexer_10_out_2;
  wire [7:0] multiplexer_4_out, multiplexer_11_out_2, multiplexer_12_out_2;
  wire [15:0] multiplexer_5_out, multiplexer_13_out, multiplexer_13_out_2, multiplexer_14_out,
       multiplexer_14_out_2;
  wire [23:0] multiplexer_11_out, multiplexer_12_out;
  wire [27:0] multiplexer_8_out, multiplexer_10_out;
  wire [29:0] multiplexer_7_out, multiplexer_9_out;
  wire [31:0] add0, and0, bsel0, mul0, mulh0, mulhu0, multiplier_1_out, or0, sll0, sra0, srl0, sub0, xor0;
  wire [31:31] multiplexer_1_out;
  wire [63:0] bit_extender_1_out, bit_extender_2_out;

  Multiplexer #(.enable("false")) multiplexer_1 (.in0(1'b0), .in1(1'b1), .out(multiplexer_1_out[31]), .sel(A[31]));
  Multiplexer #(.enable("false"), .width(2)) multiplexer_2 (
    .in0(2'b00), .in1(2'b11), .out(multiplexer_2_out), .sel(A[31]));
  Multiplexer #(.enable("false"), .width(4)) multiplexer_3 (
    .in0(4'b0000), .in1(4'b1111), .out(multiplexer_3_out), .sel(A[31]));
  Multiplexer #(.enable("false"), .width(8)) multiplexer_4 (
    .in0({8{1'b0}}), .in1({8{1'b1}}), .out(multiplexer_4_out), .sel(A[31]));
  Multiplexer #(.enable("false"), .width(16)) multiplexer_5 (
    .in0({16{1'b0}}), .in1({16{1'b1}}), .out(multiplexer_5_out), .sel(A[31]));
  Adder #(.width(32)) adder_1 (.a(A), .b(B), .out(add0));  // open: cin, cout
  assign and0 = A & B;  // AND_Gate and_1, 32 bits wide
  assign or0 = A | B;  // OR_Gate or_1, 32 bits wide
  assign xor0 = A ^ B;  // XOR_Gate xor_1, 32 bits wide
  Shifter #(.width(32)) shifter_1 (.in(A), .\dist (B[4:0]), .out(sll0));
  Comparator #(.width(32)) comparator_1 (.a(A), .b(B), .lt(slt0[0]));  // open: gt, eq
  Subtractor #(.width(32)) subtractor_1 (.a(A), .b(B), .out(sub0));  // open: bin, bout
  Multiplexer #(.enable("false"), .width(32)) multiplexer_6 (.in0(A), .in1(B), .out(bsel0), .sel(1'b1));
  assign bit_extender_1_out = {{32{A[31]}}, A};  // Bit_Extender bit_extender_1
  assign bit_extender_2_out = {{32{B[31]}}, B};  // Bit_Extender bit_extender_2
  Multiplier #(.width(64)) multiplier_1 (
    .a({{32{1'b0}}, A}), .b({{32{1'b0}}, B}), .out({mulhu0, multiplier_1_out}));  // open: cin, cout
  Multiplier #(.width(64)) multiplier_2 (
    .a(bit_extender_1_out), .b(bit_extender_2_out), .out({mulh0, mul0}));  // open: cin, cout
  Multiplexer #(.enable("false"), .width(32)) multiplexer_7 (
    .in0(A), .in1({multiplexer_1_out[31], A[31:1]}), .out({multiplexer_7_out, multiplexer_7_out_2}),
    .sel(B[0]));
  Multiplexer #(.enable("false"), .width(32)) multiplexer_8 (
    .in0({multiplexer_7_out, multiplexer_7_out_2}), .in1({multiplexer_2_out, multiplexer_7_out}),
    .out({multiplexer_8_out, multiplexer_8_out_2}), .sel(B[1]));
  Multiplexer #(.enable("false"), .width(32)) multiplexer_9 (
    .in0(A), .in1({1'b0, A[31:1]}), .out({multiplexer_9_out, multiplexer_9_out_2}), .sel(B[0]));
  Multiplexer #(.enable("false"), .width(32)) multiplexer_10 (
    .in0({multiplexer_9_out, multiplexer_9_out_2}), .in1({2'b00, multiplexer_9_out}),
    .out({multiplexer_10_out, multiplexer_10_out_2}), .sel(B[1]));
  Multiplexer #(.enable("false"), .width(32)) multiplexer_11 (
    .in0({multiplexer_8_out, multiplexer_8_out_2}), .in1({multiplexer_3_out, multiplexer_8_out}),
    .out({multiplexer_11_out, multiplexer_11_out_2}), .sel(B[2]));
  Multiplexer #(.enable("false"), .width(32)) multiplexer_12 (
    .in0({multiplexer_10_out, multiplexer_10_out_2}), .in1({4'b0000, multiplexer_10_out}),
    .out({multiplexer_12_out, multiplexer_12_out_2}), .sel(B[2]));
  Multiplexer #(.enable("false"), .width(32)) multiplexer_13 (
    .in0({multiplexer_11_out, multiplexer_11_out_2}), .in1({multiplexer_4_out, multiplexer_11_out}),
    .out({multiplexer_13_out, multiplexer_13_out_2}), .sel(B[3]));
  Multiplexer #(.enable("false"), .width(32)) multiplexer_14 (
    .in0({multiplexer_12_out, multiplexer_12_out_2}), .in1({{8{1'b0}}, multiplexer_12_out}),
    .out({multiplexer_14_out, multiplexer_14_out_2}), .sel(B[3]));
  Multiplexer #(.enable("false"), .width(32)) multiplexer_15 (
    .in0({multiplexer_13_out, multiplexer_13_out_2}), .in1({multiplexer_5_out, multiplexer_13_out}),
    .out(sra0), .sel(B[4]));
  Multiplexer #(.enable("false"), .width(32)) multiplexer_16 (
    .in0({multiplexer_14_out, multiplexer_14_out_2}), .in1({{16{1'b0}}, multiplexer_14_out}), .out(srl0),
    .sel(B[4]));
  Multiplexer #(.enable("false"), .select(4), .width(32)) multiplexer_17 (
    .in0(add0), .in1(and0), .in2(or0), .in3(xor0), .in4(srl0), .in5(sra0), .in6(sll0),
    .in7({{31{1'b0}}, slt0[0]}), .in10(mul0), .in11(mulhu0), .in12(sub0), .in13(bsel0), .in14(mulh0),
    .out(Result), .sel(ALUSel));  // open: in8, in9, in15

  // Notes on the sheet:
  //   INPUTS to your circuit
  //   DON'T CHANGE THE LOCATIONS OF THE INPUTS AND OUTPUTS!
  //   OUTPUT from your circuit
endmodule
