// Logisim project control_logic.circ as structural Verilog: 1 circuit, main circuit control_logic
module control_logic (
  input  [31:0] inst,
  input  BrEq,
  input  BrLt,
  output PCSel,
  output RegWEn,
  output [2:0] ImmSel,
  output BrUn,
  output ASel,
  output BSel,
  output [3:0] ALUSel,
  output MemRW,
  output [1:0] WBSel,
  output CSRSel,
  output CSRWen
);

  wire alu, and_1_out, B_0, B_1, B_4, B_5, B_6, B_7, Bge, Blt, ch_B, ch_jump, I, I_alg, I_jalr, I_load,
       not_1_out, not_2_out, or_8_out, or_9_out, or_10_out, PC, R, S, SB, SB_UJ, t_00, t_01, t_20, U,
       U_auipc, U_lui, UJ, write_ch;
  wire [1:0] ch_inst, multiplexer_12_out, multiplexer_17_out, multiplexer_18_out, multiplexer_19_out, op_0_ch;
  wire [2:0] multiplexer_1_out, multiplexer_3_out, multiplexer_7_out, multiplexer_9_out;
  wire [3:0] multiplexer_2_out, op, op_0, op_1, op_5;

  Multiplexer #(.enable("false"), .width(3)) multiplexer_1 (
    .in0(3'b000), .in1(3'b001), .out(multiplexer_1_out), .sel(I));
  or or_1 (alu, R, I_alg);
  Comparator #(.mode("unsigned"), .width(7)) comparator_1 (.a(inst[31:25]), .b({7{1'b0}}), .eq(t_00));  // open: gt, lt
  Comparator #(.mode("unsigned"), .width(7)) comparator_2 (.a(inst[31:25]), .b(7'b0000001), .eq(t_01));  // open: gt, lt
  Comparator #(.mode("unsigned"), .width(7)) comparator_3 (.a(inst[31:25]), .b(7'b0100000), .eq(t_20));  // open: gt, lt
  Multiplexer #(.enable("false"), .select(2), .width(4)) multiplexer_2 (
    .in0(4'b0000), .in1(4'b1010), .in2(4'b1100), .out(multiplexer_2_out), .sel(op_0_ch));  // open: in3
  or or_2 (write_ch, R, I_load, I_alg, UJ, U_auipc, U_lui, I_jalr);
  or or_3 (U, U_lui, U_auipc);
  or or_4 (I, I_load, I_alg, I_jalr);
  Multiplexer #(.enable("false"), .width(3)) multiplexer_3 (
    .in0(multiplexer_1_out), .in1(3'b010), .out(multiplexer_3_out), .sel(S));
  Multiplexer #(.enable("false"), .width(4)) multiplexer_4 (
    .in0(4'b0000), .in1(multiplexer_2_out), .out(op_0), .sel(R));
  Multiplexer #(.enable("false"), .width(4)) multiplexer_5 (.in0(4'b0110), .in1(4'b1110), .out(op_1), .sel(t_01));
  Multiplexer #(.enable("false")) multiplexer_6 (.in0(1'b0), .in1(1'b1), .out(MemRW), .sel(S));
  Multiplexer #(.enable("false"), .width(3)) multiplexer_7 (
    .in0(multiplexer_3_out), .in1(3'b011), .out(multiplexer_7_out), .sel(SB));
  Multiplexer #(.enable("false"), .select(3), .width(4)) multiplexer_8 (
    .in0(op_0), .in1(op_1), .in2(4'b0111), .in3(4'b1011), .in4(4'b0011), .in5(op_5), .in6(4'b0010),
    .in7(4'b0001), .out(op), .sel(inst[14:12]));
  Comparator #(.width(7)) comparator_4 (.a(inst[6:0]), .b(7'b0110011), .eq(R));  // open: gt, lt
  Comparator #(.width(7)) comparator_5 (.a(inst[6:0]), .b(7'b0000011), .eq(I_load));  // open: gt, lt
  Comparator #(.width(7)) comparator_6 (.a(inst[6:0]), .b(7'b0010011), .eq(I_alg));  // open: gt, lt
  Comparator #(.width(7)) comparator_7 (.a(inst[6:0]), .b(7'b0100011), .eq(S));  // open: gt, lt
  Comparator #(.width(7)) comparator_8 (.a(inst[6:0]), .b(7'b1100011), .eq(SB));  // open: gt, lt
  Comparator #(.width(7)) comparator_9 (.a(inst[6:0]), .b(7'b0010111), .eq(U_auipc));  // open: gt, lt
  Comparator #(.width(7)) comparator_10 (.a(inst[6:0]), .b(7'b0110111), .eq(U_lui));  // open: gt, lt
  Comparator #(.width(7)) comparator_11 (.a(inst[6:0]), .b(7'b1101111), .eq(UJ));  // open: gt, lt
  Comparator #(.width(7)) comparator_12 (.a(inst[6:0]), .b(7'b1100111), .eq(I_jalr));  // open: gt, lt
  Comparator #(.width(7)) comparator_13 (.a(inst[6:0]), .b(7'b1110011), .eq(CSRSel));  // open: gt, lt
  Multiplexer #(.enable("false"), .width(3)) multiplexer_9 (
    .in0(multiplexer_7_out), .in1(3'b100), .out(multiplexer_9_out), .sel(U));
  Multiplexer #(.enable("false"), .width(3)) multiplexer_10 (
    .in0(multiplexer_9_out), .in1(3'b101), .out(ImmSel), .sel(UJ));
  Multiplexer #(.enable("false"), .width(4)) multiplexer_11 (.in0(4'b0000), .in1(op), .out(ALUSel), .sel(alu));
  Multiplexer #(.enable("false"), .width(2)) multiplexer_12 (
    .in0(2'b00), .in1(2'b01), .out(multiplexer_12_out), .sel(t_01));
  Multiplexer #(.enable("false")) multiplexer_13 (.in0(1'b0), .in1(1'b1), .out(RegWEn), .sel(write_ch));
  Multiplexer #(.enable("false"), .width(2)) multiplexer_14 (
    .in0(multiplexer_12_out), .in1(2'b10), .out(op_0_ch), .sel(t_20));
  Multiplexer #(.enable("false"), .width(4)) multiplexer_15 (.in0(4'b0100), .in1(4'b0101), .out(op_5), .sel(t_20));
  or or_5 (BSel, I, S, SB, U, UJ);
  and and_1 (and_1_out, SB, ch_jump);
  or or_6 (SB_UJ, SB, UJ);
  Multiplexer #(.enable("false")) multiplexer_16 (.in0(1'b1), .in1(ch_B), .out(ch_jump), .sel(SB));
  Comparator #(.mode("unsigned"), .width(3)) comparator_14 (.a(inst[14:12]), .b(3'b000), .eq(B_0));  // open: gt, lt
  Comparator #(.mode("unsigned"), .width(3)) comparator_15 (.a(inst[14:12]), .b(3'b001), .eq(B_1));  // open: gt, lt
  Comparator #(.mode("unsigned"), .width(3)) comparator_16 (.a(inst[14:12]), .b(3'b100), .eq(B_4));  // open: gt, lt
  Comparator #(.mode("unsigned"), .width(3)) comparator_17 (.a(inst[14:12]), .b(3'b101), .eq(B_5));  // open: gt, lt
  Comparator #(.mode("unsigned"), .width(3)) comparator_18 (.a(inst[14:12]), .b(3'b110), .eq(B_6));  // open: gt, lt
  Comparator #(.mode("unsigned"), .width(3)) comparator_19 (.a(inst[14:12]), .b(3'b111), .eq(B_7));  // open: gt, lt
  Multiplexer #(.enable("false"), .width(2)) multiplexer_17 (
    .in0(2'b00), .in1(2'b01), .out(multiplexer_17_out), .sel(B_1));
  Multiplexer #(.enable("false"), .width(2)) multiplexer_18 (
    .in0(2'b01), .in1(2'b00), .out(multiplexer_18_out), .sel(I_load));
  or or_7 (PC, and_1_out, UJ, I_jalr);
  Multiplexer #(.enable("false"), .width(2)) multiplexer_19 (
    .in0(multiplexer_17_out), .in1(2'b10), .out(multiplexer_19_out), .sel(Blt));
  Multiplexer #(.enable("false"), .width(2)) multiplexer_20 (
    .in0(multiplexer_18_out), .in1(2'b10), .out(WBSel), .sel(or_8_out));
  or or_8 (or_8_out, UJ, I_jalr);
  Multiplexer #(.enable("false"), .width(2)) multiplexer_21 (
    .in0(multiplexer_19_out), .in1(2'b11), .out(ch_inst), .sel(Bge));
  Multiplexer #(.enable("false")) multiplexer_22 (.in0(1'b0), .in1(1'b1), .out(PCSel), .sel(PC));
  Multiplexer #(.enable("false")) multiplexer_23 (.in0(1'b0), .in1(ch_jump), .out(ASel), .sel(or_9_out));
  or or_9 (or_9_out, U_auipc, SB_UJ);
  not not_1 (not_1_out, BrEq);
  not not_2 (not_2_out, BrLt);
  or or_10 (or_10_out, B_6, B_7);
  or or_11 (Blt, B_4, B_6);
  or or_12 (Bge, B_5, B_7);
  Multiplexer #(.enable("false")) multiplexer_24 (.in0(1'b0), .in1(1'b1), .out(BrUn), .sel(or_10_out));
  Multiplexer #(.enable("false"), .select(2)) multiplexer_25 (
    .in0(BrEq), .in1(not_1_out), .in2(BrLt), .in3(not_2_out), .out(ch_B), .sel(ch_inst));

  assign CSRWen = CSRSel;

  // Other names for the same wires on the sheet: I_csr = CSRSel; opcode[6:0] = inst[6:0]; funct3[2:0] = inst[14:12];
  //   funct7[6:0] = inst[31:25]

  // Notes on the sheet:
  //   INPUTS to your circuit
  //   DON'T CHANGE THE LOCATIONS OF THE INPUTS AND OUTPUTS!
  //   OUTPUT from your circuit
endmodule
