// Logisim project cpu.circ as structural Verilog: 1 circuit, main circuit cpu
module cpu (
  input  clk,
  input  [31:0] INSTRUCTION,
  input  [31:0] READ_DATA,
  output [31:0] WRITE_ADDRESS,
  output [31:0] PROGRAM_COUNTER,
  output [31:0] ra,
  output [31:0] sp,
  output [31:0] t0,
  output [31:0] t1,
  output [31:0] t2,
  output [31:0] s0,
  output [31:0] s1,
  output [31:0] a0,
  output [31:0] tohost,
  output [3:0] WRITE_ENABLE,
  output [31:0] WRITE_DATA
);

  wire ASel, BrEq, BrLt, BrUn, BSel, \byte , csr_i, csr_r, CSRSel, CSRWen, half_word, MemRW, PCSel, RegWEn,
       word;
  wire [1:0] and_1_out, bit_extender_2_out, ch_bit, multiplexer_6_out, multiplexer_9_out, WBSel;
  wire [2:0] funct3, ImmSel;
  wire [3:0] ALUSel;
  wire [11:0] csr_address;
  wire [19:0] inst_new;
  wire [31:0] adder_1_out, adder_2_out, bit_extender_1_out, bit_extender_3_out, bit_extender_4_out, data1,
       imm, multiplexer_1_out, multiplexer_2_out, multiplexer_3_out, multiplexer_4_out, multiplexer_5_out,
       multiplexer_7_out, multiplexer_10_out, pc_new, read_result, WB;

  Adder #(.width(32)) adder_1 (.a(PROGRAM_COUNTER), .b(32'h4), .out(adder_1_out));  // open: cin, cout
  Multiplexer #(.enable("false"), .width(32)) multiplexer_1 (
    .in0(adder_1_out), .in1(WRITE_ADDRESS), .out(multiplexer_1_out), .sel(PCSel));
  Register #(.width(32)) PC (.D(multiplexer_1_out), .clk(clk), .Q(PROGRAM_COUNTER));  // open: en, clr
  Multiplexer #(.enable("false"), .width(32)) multiplexer_2 (
    .in0(INSTRUCTION), .in1(32'h13), .out(multiplexer_2_out), .sel(PCSel));
  Register #(.width(32)) register_1 (.D(PROGRAM_COUNTER), .clk(clk), .Q(pc_new));  // open: en, clr
  Register #(.width(32)) register_2 (
    .D(multiplexer_2_out), .clk(clk), .Q({csr_address, inst_new[19:15], funct3, inst_new[11:0]}));  // open: en, clr
  control_logic control_logic_1 (
    .CSRWen(CSRWen), .PCSel(PCSel), .RegWEn(RegWEn), .ImmSel(ImmSel), .BrUn(BrUn), .ASel(ASel), .BSel(BSel),
    .ALUSel(ALUSel), .MemRW(MemRW), .WBSel(WBSel), .CSRSel(CSRSel),
    .inst({csr_address, inst_new[19:15], funct3, inst_new[11:0]}), .BrEq(BrEq), .BrLt(BrLt));
  Comparator #(.mode("unsigned"), .width(3)) comparator_1 (.a(funct3), .b(3'b001), .eq(csr_r));  // open: gt, lt
  Comparator #(.mode("unsigned"), .width(3)) comparator_2 (.a(funct3), .b(3'b101), .eq(csr_i));  // open: gt, lt
  imm_gen imm_gen_1 (.inst({csr_address, inst_new[19:15], funct3, inst_new[11:0]}), .ImmSel(ImmSel), .imm(imm));
  regfile regfile_1 (
    .rs1(inst_new[19:15]), .rs2(csr_address[4:0]), .rd(inst_new[11:7]), .Write_Data(WB), .RegWEn(RegWEn),
    .clk(clk), .ra(ra), .sp(sp), .t0(t0), .t1(t1), .t2(t2), .s0(s0), .s1(s1), .a0(a0), .Read_Data_1(data1),
    .Read_Data_2(WRITE_DATA));
  branch_comp branch_comp_1 (.rs1(data1), .rs2(WRITE_DATA), .BrUn(BrUn), .BrEq(BrEq), .BrLt(BrLt));
  csr csr_1 (.CSR_address(csr_address), .CSR_din(WRITE_ADDRESS), .CSR_WE(CSRWen), .clk(clk), .tohost(tohost));
  assign bit_extender_1_out = {{27{1'b0}}, inst_new[19:15]};  // Bit_Extender bit_extender_1
  Multiplexer #(.enable("false"), .width(32)) multiplexer_3 (
    .in0(data1), .in1(pc_new), .out(multiplexer_3_out), .sel(ASel));
  Multiplexer #(.enable("false"), .width(32)) multiplexer_4 (
    .in0(data1), .in1(bit_extender_1_out), .out(multiplexer_4_out), .sel(csr_i));
  Multiplexer #(.enable("false"), .width(32)) multiplexer_5 (
    .in0(WRITE_DATA), .in1(imm), .out(multiplexer_5_out), .sel(BSel));
  assign and_1_out = bit_extender_2_out & ch_bit;  // AND_Gate and_1, 2 bits wide
  assign bit_extender_2_out = {{1{MemRW}}, MemRW};  // Bit_Extender bit_extender_2
  Comparator #(.mode("unsigned"), .width(3)) comparator_3 (.a(funct3), .b(3'b000), .eq(\byte ));  // open: gt, lt
  Comparator #(.mode("unsigned"), .width(3)) comparator_4 (.a(funct3), .b(3'b001), .eq(half_word));  // open: gt, lt
  Comparator #(.mode("unsigned"), .width(3)) comparator_5 (.a(funct3), .b(3'b010), .eq(word));  // open: gt, lt
  Multiplexer #(.enable("false"), .width(2)) multiplexer_6 (
    .in0(2'b00), .in1(2'b01), .out(multiplexer_6_out), .sel(\byte ));
  Multiplexer #(.enable("false"), .width(32)) multiplexer_7 (
    .in0(multiplexer_3_out), .in1(multiplexer_4_out), .out(multiplexer_7_out), .sel(CSRSel));
  Multiplexer #(.enable("false"), .select(2), .width(4)) multiplexer_8 (
    .in0(4'b0000), .in1(4'b0001), .in2(4'b0011), .in3(4'b1111), .out(WRITE_ENABLE), .sel(and_1_out));
  Multiplexer #(.enable("false"), .width(2)) multiplexer_9 (
    .in0(multiplexer_6_out), .in1(2'b10), .out(multiplexer_9_out), .sel(half_word));
  Multiplexer #(.enable("false"), .width(32)) multiplexer_10 (
    .in0(multiplexer_5_out), .in1(tohost), .out(multiplexer_10_out), .sel(CSRSel));
  Multiplexer #(.enable("false"), .width(2)) multiplexer_11 (
    .in0(multiplexer_9_out), .in1(2'b11), .out(ch_bit), .sel(word));
  alu alu_1 (.Result(WRITE_ADDRESS), .A(multiplexer_7_out), .B(multiplexer_10_out), .ALUSel(ALUSel));
  Adder #(.width(32)) adder_2 (.a(pc_new), .b(32'h4), .out(adder_2_out));  // open: cin, cout
  assign bit_extender_3_out = {{24{READ_DATA[7]}}, READ_DATA[7:0]};  // Bit_Extender bit_extender_3
  assign bit_extender_4_out = {{16{READ_DATA[15]}}, READ_DATA[15:0]};  // Bit_Extender bit_extender_4
  Multiplexer #(.enable("false"), .select(2), .width(32)) multiplexer_12 (
    .in0(read_result), .in1(WRITE_ADDRESS), .in2(adder_2_out), .out(WB), .sel(WBSel));  // open: in3
  Multiplexer #(.enable("false"), .select(2), .width(32)) multiplexer_13 (
    .in0(READ_DATA), .in1(bit_extender_3_out), .in2(bit_extender_4_out), .in3(READ_DATA), .out(read_result),
    .sel(ch_bit));

  // Other names for the same wires on the sheet: alu_result[31:0] = WRITE_ADDRESS;
  //   inst_new (some bits) = {csr_address, funct3}; rs2[4:0] = csr_address[4:0]; funct7[6:0] = csr_address[11:5];
  //   data2[31:0] = WRITE_DATA; opcode[6:0] = inst_new[6:0]; rd[4:0] = inst_new[11:7]; rs1[4:0] = inst_new[19:15];
  //   lb[7:0] = READ_DATA[7:0]; lh[15:0] = READ_DATA[15:0]; lw[31:0] = READ_DATA

  // Notes on the sheet:
  //   Output to IMEM
  //   IMEM (do **NOT** move this)
  //   Inputs from IMEM
  //   It is OK to move the PC, RegFile, ALU, MEM, Branch Comp, Imm Gen, and Control Logic to wherever is most convenient for you when constructing your CPU, and to delete this text
  //   Inputs/Outputs for testing. Do **NOT** move these.
  //   Outputs To DMEM
  //   DMEM (do **NOT** move this)
  //   Inputs From DMEM
endmodule
