// Logisim project csr.circ as structural Verilog: 1 circuit, main circuit csr
module csr (
  input  [11:0] CSR_address,
  input  [31:0] CSR_din,
  input  CSR_WE,
  input  clk,
  input  in_5,
  output [31:0] tohost
);

  wire and_1_out, jd;
  wire [31:0] multiplexer_1_out;

  Comparator #(.mode("unsigned"), .width(12)) comparator_1 (.a(CSR_address), .b(12'h51e), .eq(jd));  // open: gt, lt
  Multiplexer #(.enable("false"), .width(32)) multiplexer_1 (
    .in0(tohost), .in1(CSR_din), .out(multiplexer_1_out), .sel(and_1_out));
  and and_1 (and_1_out, jd, CSR_WE);
  Register #(.width(32)) register_1 (.D(multiplexer_1_out), .clk(in_5), .Q(tohost));  // open: en, clr

  // Other names for the same wires on the sheet: address[11:0] = CSR_address; data[31:0] = CSR_din; WE = CSR_WE

  // Notes on the sheet:
  //   INPUTS to your circuit
  //   DON'T CHANGE THE LOCATIONS OF THE INPUTS AND OUTPUTS!
  //   OUTPUT from your circuit
endmodule
