// Logisim project imm_gen.circ as structural Verilog: 1 circuit, main circuit imm_gen
module imm_gen (
  input  [31:0] inst,
  input  [2:0] ImmSel,
  output [31:0] imm
);

  wire I, S, S_SB, SB, SB_U_UJ, U, U_UJ, UJ;
  wire [1:0] multiplexer_1_out, multiplexer_2_out, multiplexer_3_out, multiplexer_4_out, multiplexer_6_out,
       multiplexer_7_out, multiplexer_8_out;
  wire [7:0] inst_31_19_12;
  wire [10:0] inst_31_30_20;

  Demultiplexer #(.enable("false"), .select(3)) demultiplexer_1 (
    .out1(I), .out2(S), .out3(SB), .out4(U), .out5(UJ), .in(1'b1), .sel(ImmSel));  // open: out0, out6, out7
  assign {inst_31_30_20, inst_31_19_12} = {{18{inst[31]}}, inst[31]};  // Bit_Extender bit_extender_1
  Multiplexer #(.enable("false"), .width(2)) multiplexer_1 (.in0(2'b00), .in1(2'b01), .out(multiplexer_1_out), .sel(S));
  Multiplexer #(.enable("false"), .width(2)) multiplexer_2 (
    .in0(multiplexer_1_out), .in1(2'b10), .out(multiplexer_2_out), .sel(SB_U_UJ));
  Multiplexer #(.enable("false"), .width(2)) multiplexer_3 (
    .in0(2'b00), .in1(2'b01), .out(multiplexer_3_out), .sel(S_SB));
  Multiplexer #(.enable("false"), .width(2)) multiplexer_4 (
    .in0(2'b00), .in1(2'b01), .out(multiplexer_4_out), .sel(SB));
  or or_1 (S_SB, S, SB);
  or or_2 (SB_U_UJ, SB, U_UJ);
  Multiplexer #(.enable("false"), .select(2)) multiplexer_5 (
    .in0(inst[20]), .in1(inst[7]), .in2(1'b0), .out(imm[0]), .sel(multiplexer_2_out));  // open: in3
  Multiplexer #(.enable("false"), .width(2)) multiplexer_6 (
    .in0(multiplexer_3_out), .in1(2'b10), .out(multiplexer_6_out), .sel(U));
  Multiplexer #(.enable("false"), .width(2)) multiplexer_7 (
    .in0(multiplexer_4_out), .in1(2'b10), .out(multiplexer_7_out), .sel(U));
  Multiplexer #(.enable("false"), .width(2)) multiplexer_8 (
    .in0(multiplexer_7_out), .in1(2'b11), .out(multiplexer_8_out), .sel(UJ));
  Multiplexer #(.enable("false"), .select(2), .width(4)) multiplexer_9 (
    .in0(inst[24:21]), .in1(inst[11:8]), .in2(4'b0000), .out(imm[4:1]), .sel(multiplexer_6_out));  // open: in3
  Multiplexer #(.enable("false"), .select(2)) multiplexer_10 (
    .in0(inst[31]), .in1(inst[7]), .in2(1'b0), .in3(inst[20]), .out(imm[11]), .sel(multiplexer_8_out));
  or or_3 (U_UJ, U, UJ);
  Multiplexer #(.enable("false"), .width(6)) multiplexer_11 (
    .in0(inst[30:25]), .in1({6{1'b0}}), .out(imm[10:5]), .sel(U));
  Multiplexer #(.enable("false"), .width(8)) multiplexer_12 (
    .in0(inst_31_19_12), .in1(inst[19:12]), .out(imm[19:12]), .sel(U_UJ));
  Multiplexer #(.enable("false"), .width(11)) multiplexer_13 (
    .in0(inst_31_30_20), .in1(inst[30:20]), .out(imm[30:20]), .sel(U));

  assign imm[31] = inst[31];

  // Other names for the same wires on the sheet: ch0 = imm[0]; ch1[3:0] = imm[4:1]; ch2[5:0] = imm[10:5];
  //   ch3 = imm[11]; ch4[7:0] = imm[19:12]; ch5[10:0] = imm[30:20]; inst11_8[3:0] = inst[11:8];
  //   inst19_12[7:0] = inst[19:12]; inst30_20[10:0] = inst[30:20]; inst24_21[3:0] = inst[24:21];
  //   inst30_25[5:0] = inst[30:25]

  // Notes on the sheet:
  //   INPUTS to your circuit
  //   DON'T CHANGE THE LOCATIONS OF THE INPUTS AND OUTPUTS!
  //   OUTPUT from your circuit
endmodule
