// Logisim project regfile.circ as structural Verilog: 1 circuit, main circuit regfile
module regfile (
  input  [4:0] rs1,
  input  [4:0] rs2,
  input  [4:0] rd,
  input  [31:0] Write_Data,
  input  RegWEn,
  input  clk,
  output [31:0] ra,
  output [31:0] sp,
  output [31:0] t0,
  output [31:0] t1,
  output [31:0] t2,
  output [31:0] s0,
  output [31:0] s1,
  output [31:0] a0,
  output [31:0] Read_Data_1,
  output [31:0] Read_Data_2
);

  wire and_1_out, and_2_out, and_3_out, and_4_out, and_5_out, and_6_out, and_7_out, and_8_out, and_9_out,
       and_10_out, and_11_out, and_12_out, and_13_out, and_14_out, and_15_out, and_16_out, and_17_out,
       and_18_out, and_19_out, and_20_out, and_21_out, and_22_out, and_23_out, and_24_out, and_25_out,
       and_26_out, and_27_out, and_28_out, and_29_out, and_30_out, and_31_out, and_32_out, ch0, ch1, ch2,
       ch3, ch4, ch5, ch6, ch7, ch8, ch9, ch10, ch11, ch12, ch13, ch14, ch15, ch16, ch17, ch18, ch19, ch20,
       ch21, ch22, ch23, ch24, ch25, ch26, ch27, ch28, ch29, ch30, ch31;
  wire [31:0] multiplexer_3_out, multiplexer_4_out, multiplexer_5_out, multiplexer_6_out, multiplexer_7_out,
       multiplexer_8_out, multiplexer_9_out, multiplexer_10_out, multiplexer_11_out, multiplexer_12_out,
       multiplexer_13_out, multiplexer_14_out, multiplexer_15_out, multiplexer_16_out, multiplexer_17_out,
       multiplexer_18_out, multiplexer_19_out, multiplexer_20_out, multiplexer_21_out, multiplexer_22_out,
       multiplexer_23_out, multiplexer_24_out, multiplexer_25_out, multiplexer_26_out, multiplexer_27_out,
       multiplexer_28_out, multiplexer_29_out, multiplexer_30_out, multiplexer_31_out, multiplexer_32_out,
       multiplexer_33_out, multiplexer_34_out, x0, x3, x4, x11, x12, x13, x14, x15, x16, x17, x18, x19, x20,
       x21, x22, x23, x24, x25, x26, x27, x28, x29, x30, x31;

  Multiplexer #(.enable("false"), .select(5), .width(32)) multiplexer_1 (
    .in0(x0), .in1(ra), .in2(sp), .in3(x3), .in4(x4), .in5(t0), .in6(t1), .in7(t2), .in8(s0), .in9(s1),
    .in10(a0), .in11(x11), .in12(x12), .in13(x13), .in14(x14), .in15(x15), .in16(x16), .in17(x17),
    .in18(x18), .in19(x19), .in20(x20), .in21(x21), .in22(x22), .in23(x23), .in24(x24), .in25(x25),
    .in26(x26), .in27(x27), .in28(x28), .in29(x29), .in30(x30), .in31(x31), .out(Read_Data_1), .sel(rs1));
  Multiplexer #(.enable("false"), .select(5), .width(32)) multiplexer_2 (
    .in0(x0), .in1(ra), .in2(sp), .in3(x3), .in4(x4), .in5(t0), .in6(t1), .in7(t2), .in8(s0), .in9(s1),
    .in10(a0), .in11(x11), .in12(x12), .in13(x13), .in14(x14), .in15(x15), .in16(x16), .in17(x17),
    .in18(x18), .in19(x19), .in20(x20), .in21(x21), .in22(x22), .in23(x23), .in24(x24), .in25(x25),
    .in26(x26), .in27(x27), .in28(x28), .in29(x29), .in30(x30), .in31(x31), .out(Read_Data_2), .sel(rs2));
  Demultiplexer #(.enable("false"), .select(5)) demultiplexer_1 (
    .out0(ch0), .out1(ch1), .out2(ch2), .out3(ch3), .out4(ch4), .out5(ch5), .out6(ch6), .out7(ch7),
    .out8(ch8), .out9(ch9), .out10(ch10), .out11(ch11), .out12(ch12), .out13(ch13), .out14(ch14),
    .out15(ch15), .out16(ch16), .out17(ch17), .out18(ch18), .out19(ch19), .out20(ch20), .out21(ch21),
    .out22(ch22), .out23(ch23), .out24(ch24), .out25(ch25), .out26(ch26), .out27(ch27), .out28(ch28),
    .out29(ch29), .out30(ch30), .out31(ch31), .in(1'b1), .sel(rd));
  and and_1 (and_1_out, 1'b0, ch0);
  Multiplexer #(.enable("false"), .width(32)) multiplexer_3 (
    .in0(x0), .in1(Write_Data), .out(multiplexer_3_out), .sel(and_1_out));
  Multiplexer #(.enable("false"), .width(32)) multiplexer_4 (
    .in0(ra), .in1(Write_Data), .out(multiplexer_4_out), .sel(and_2_out));
  and and_2 (and_2_out, RegWEn, ch1);
  Multiplexer #(.enable("false"), .width(32)) multiplexer_5 (
    .in0(sp), .in1(Write_Data), .out(multiplexer_5_out), .sel(and_3_out));
  and and_3 (and_3_out, RegWEn, ch2);
  Multiplexer #(.enable("false"), .width(32)) multiplexer_6 (
    .in0(x3), .in1(Write_Data), .out(multiplexer_6_out), .sel(and_4_out));
  and and_4 (and_4_out, RegWEn, ch3);
  Multiplexer #(.enable("false"), .width(32)) multiplexer_7 (
    .in0(x4), .in1(Write_Data), .out(multiplexer_7_out), .sel(and_5_out));
  and and_5 (and_5_out, RegWEn, ch4);
  Multiplexer #(.enable("false"), .width(32)) multiplexer_8 (
    .in0(t0), .in1(Write_Data), .out(multiplexer_8_out), .sel(and_6_out));
  and and_6 (and_6_out, RegWEn, ch5);
  Multiplexer #(.enable("false"), .width(32)) multiplexer_9 (
    .in0(t1), .in1(Write_Data), .out(multiplexer_9_out), .sel(and_7_out));
  and and_7 (and_7_out, RegWEn, ch6);
  Multiplexer #(.enable("false"), .width(32)) multiplexer_10 (
    .in0(t2), .in1(Write_Data), .out(multiplexer_10_out), .sel(and_8_out));
  and and_8 (and_8_out, RegWEn, ch7);
  Register #(.width(32)) u_x0 (.D(multiplexer_3_out), .clk(clk), .Q(x0));  // open: en, clr
  Register #(.width(32)) x1 (.D(multiplexer_4_out), .clk(clk), .Q(ra));  // open: en, clr
  Register #(.width(32)) x2 (.D(multiplexer_5_out), .clk(clk), .Q(sp));  // open: en, clr
  Register #(.width(32)) u_x3 (.D(multiplexer_6_out), .clk(clk), .Q(x3));  // open: en, clr
  Register #(.width(32)) u_x4 (.D(multiplexer_7_out), .clk(clk), .Q(x4));  // open: en, clr
  Register #(.width(32)) x5 (.D(multiplexer_8_out), .clk(clk), .Q(t0));  // open: en, clr
  Register #(.width(32)) x6 (.D(multiplexer_9_out), .clk(clk), .Q(t1));  // open: en, clr
  Register #(.width(32)) x7 (.D(multiplexer_10_out), .clk(clk), .Q(t2));  // open: en, clr
  Multiplexer #(.enable("false"), .width(32)) multiplexer_11 (
    .in0(s0), .in1(Write_Data), .out(multiplexer_11_out), .sel(and_9_out));
  and and_9 (and_9_out, RegWEn, ch8);
  and and_10 (and_10_out, RegWEn, ch9);
  and and_11 (and_11_out, RegWEn, ch10);
  and and_12 (and_12_out, RegWEn, ch11);
  and and_13 (and_13_out, RegWEn, ch12);
  and and_14 (and_14_out, RegWEn, ch13);
  and and_15 (and_15_out, RegWEn, ch14);
  and and_16 (and_16_out, RegWEn, ch15);
  Multiplexer #(.enable("false"), .width(32)) multiplexer_12 (
    .in0(s1), .in1(Write_Data), .out(multiplexer_12_out), .sel(and_10_out));
  Multiplexer #(.enable("false"), .width(32)) multiplexer_13 (
    .in0(a0), .in1(Write_Data), .out(multiplexer_13_out), .sel(and_11_out));
  Multiplexer #(.enable("false"), .width(32)) multiplexer_14 (
    .in0(x11), .in1(Write_Data), .out(multiplexer_14_out), .sel(and_12_out));
  Multiplexer #(.enable("false"), .width(32)) multiplexer_15 (
    .in0(x12), .in1(Write_Data), .out(multiplexer_15_out), .sel(and_13_out));
  Multiplexer #(.enable("false"), .width(32)) multiplexer_16 (
    .in0(x13), .in1(Write_Data), .out(multiplexer_16_out), .sel(and_14_out));
  Multiplexer #(.enable("false"), .width(32)) multiplexer_17 (
    .in0(x14), .in1(Write_Data), .out(multiplexer_17_out), .sel(and_15_out));
  Multiplexer #(.enable("false"), .width(32)) multiplexer_18 (
    .in0(x15), .in1(Write_Data), .out(multiplexer_18_out), .sel(and_16_out));
  Register #(.width(32)) x8 (.D(multiplexer_11_out), .clk(clk), .Q(s0));  // open: en, clr
  Register #(.width(32)) x9 (.D(multiplexer_12_out), .clk(clk), .Q(s1));  // open: en, clr
  Register #(.width(32)) x10 (.D(multiplexer_13_out), .clk(clk), .Q(a0));  // open: en, clr
  Register #(.width(32)) u_x11 (.D(multiplexer_14_out), .clk(clk), .Q(x11));  // open: en, clr
  Register #(.width(32)) u_x12 (.D(multiplexer_15_out), .clk(clk), .Q(x12));  // open: en, clr
  Register #(.width(32)) u_x13 (.D(multiplexer_16_out), .clk(clk), .Q(x13));  // open: en, clr
  Register #(.width(32)) u_x14 (.D(multiplexer_17_out), .clk(clk), .Q(x14));  // open: en, clr
  Register #(.width(32)) u_x15 (.D(multiplexer_18_out), .clk(clk), .Q(x15));  // open: en, clr
  Multiplexer #(.enable("false"), .width(32)) multiplexer_19 (
    .in0(x16), .in1(Write_Data), .out(multiplexer_19_out), .sel(and_17_out));
  and and_17 (and_17_out, RegWEn, ch16);
  Multiplexer #(.enable("false"), .width(32)) multiplexer_20 (
    .in0(x17), .in1(Write_Data), .out(multiplexer_20_out), .sel(and_18_out));
  and and_18 (and_18_out, RegWEn, ch17);
  Multiplexer #(.enable("false"), .width(32)) multiplexer_21 (
    .in0(x18), .in1(Write_Data), .out(multiplexer_21_out), .sel(and_19_out));
  and and_19 (and_19_out, RegWEn, ch18);
  Multiplexer #(.enable("false"), .width(32)) multiplexer_22 (
    .in0(x19), .in1(Write_Data), .out(multiplexer_22_out), .sel(and_20_out));
  and and_20 (and_20_out, RegWEn, ch19);
  Multiplexer #(.enable("false"), .width(32)) multiplexer_23 (
    .in0(x20), .in1(Write_Data), .out(multiplexer_23_out), .sel(and_21_out));
  and and_21 (and_21_out, RegWEn, ch20);
  Multiplexer #(.enable("false"), .width(32)) multiplexer_24 (
    .in0(x21), .in1(Write_Data), .out(multiplexer_24_out), .sel(and_22_out));
  and and_22 (and_22_out, RegWEn, ch21);
  Multiplexer #(.enable("false"), .width(32)) multiplexer_25 (
    .in0(x22), .in1(Write_Data), .out(multiplexer_25_out), .sel(and_23_out));
  and and_23 (and_23_out, RegWEn, ch22);
  Multiplexer #(.enable("false"), .width(32)) multiplexer_26 (
    .in0(x23), .in1(Write_Data), .out(multiplexer_26_out), .sel(and_24_out));
  and and_24 (and_24_out, RegWEn, ch23);
  Register #(.width(32)) u_x16 (.D(multiplexer_19_out), .clk(clk), .Q(x16));  // open: en, clr
  Register #(.width(32)) u_x17 (.D(multiplexer_20_out), .clk(clk), .Q(x17));  // open: en, clr
  Register #(.width(32)) u_x18 (.D(multiplexer_21_out), .clk(clk), .Q(x18));  // open: en, clr
  Register #(.width(32)) u_x19 (.D(multiplexer_22_out), .clk(clk), .Q(x19));  // open: en, clr
  Register #(.width(32)) u_x20 (.D(multiplexer_23_out), .clk(clk), .Q(x20));  // open: en, clr
  Register #(.width(32)) u_x21 (.D(multiplexer_24_out), .clk(clk), .Q(x21));  // open: en, clr
  Register #(.width(32)) u_x22 (.D(multiplexer_25_out), .clk(clk), .Q(x22));  // open: en, clr
  Register #(.width(32)) u_x23 (.D(multiplexer_26_out), .clk(clk), .Q(x23));  // open: en, clr
  and and_25 (and_25_out, RegWEn, ch24);
  Multiplexer #(.enable("false"), .width(32)) multiplexer_27 (
    .in0(x24), .in1(Write_Data), .out(multiplexer_27_out), .sel(and_25_out));
  Multiplexer #(.enable("false"), .width(32)) multiplexer_28 (
    .in0(x25), .in1(Write_Data), .out(multiplexer_28_out), .sel(and_26_out));
  and and_26 (and_26_out, RegWEn, ch25);
  Multiplexer #(.enable("false"), .width(32)) multiplexer_29 (
    .in0(x26), .in1(Write_Data), .out(multiplexer_29_out), .sel(and_27_out));
  and and_27 (and_27_out, RegWEn, ch26);
  Multiplexer #(.enable("false"), .width(32)) multiplexer_30 (
    .in0(x27), .in1(Write_Data), .out(multiplexer_30_out), .sel(and_28_out));
  and and_28 (and_28_out, RegWEn, ch27);
  Multiplexer #(.enable("false"), .width(32)) multiplexer_31 (
    .in0(x28), .in1(Write_Data), .out(multiplexer_31_out), .sel(and_29_out));
  and and_29 (and_29_out, RegWEn, ch28);
  Multiplexer #(.enable("false"), .width(32)) multiplexer_32 (
    .in0(x29), .in1(Write_Data), .out(multiplexer_32_out), .sel(and_30_out));
  and and_30 (and_30_out, RegWEn, ch29);
  Multiplexer #(.enable("false"), .width(32)) multiplexer_33 (
    .in0(x30), .in1(Write_Data), .out(multiplexer_33_out), .sel(and_31_out));
  and and_31 (and_31_out, RegWEn, ch30);
  Multiplexer #(.enable("false"), .width(32)) multiplexer_34 (
    .in0(x31), .in1(Write_Data), .out(multiplexer_34_out), .sel(and_32_out));
  and and_32 (and_32_out, RegWEn, ch31);
  Register #(.width(32)) u_x24 (.D(multiplexer_27_out), .clk(clk), .Q(x24));  // open: en, clr
  Register #(.width(32)) u_x25 (.D(multiplexer_28_out), .clk(clk), .Q(x25));  // open: en, clr
  Register #(.width(32)) u_x26 (.D(multiplexer_29_out), .clk(clk), .Q(x26));  // open: en, clr
  Register #(.width(32)) u_x27 (.D(multiplexer_30_out), .clk(clk), .Q(x27));  // open: en, clr
  Register #(.width(32)) u_x28 (.D(multiplexer_31_out), .clk(clk), .Q(x28));  // open: en, clr
  Register #(.width(32)) u_x29 (.D(multiplexer_32_out), .clk(clk), .Q(x29));  // open: en, clr
  Register #(.width(32)) u_x30 (.D(multiplexer_33_out), .clk(clk), .Q(x30));  // open: en, clr
  Register #(.width(32)) u_x31 (.D(multiplexer_34_out), .clk(clk), .Q(x31));  // open: en, clr

  // Other names for the same wires on the sheet: read_data1[31:0] = Read_Data_1; read_data2[31:0] = Read_Data_2;
  //   read_reg1[4:0] = rs1; read_reg2[4:0] = rs2; write_en = RegWEn; write_reg[4:0] = rd; x1[31:0] = ra;
  //   x2[31:0] = sp; x5[31:0] = t0; x6[31:0] = t1; x7[31:0] = t2; x8[31:0] = s0; x9[31:0] = s1; x10[31:0] = a0

  // Notes on the sheet:
  //   INPUTS to your circuit
  //   DON'T CHANGE THE LOCATIONS OF THE INPUTS AND OUTPUTS!
  //   These are DEBUG/TEST outputs from your circuit.
  //   OUTPUTS from your circuit
endmodule
